// Digital circuit MMU.dig as structural Verilog
module MMU (
  input  [31:0] Din,
  input  [31:0] Ain,
  input  [3:0] ByteSelect,
  input  Clock,
  input  We,
  output [31:0] Dout
);

  wire and_1_out, and_2_out, and_3_out, nor_1_out;

  nor nor_1 (nor_1_out, Ain[18], Ain[19], Ain[20], Ain[21], Ain[22], Ain[23], Ain[24], Ain[25], Ain[26], Ain[27], Ain[28], Ain[29], Ain[30], Ain[31]);
  and and_1 (and_1_out, ~Ain[12], ~Ain[13], ~Ain[14], ~Ain[15], ~Ain[16], ~Ain[17], ~Ain[18], ~Ain[19], ~Ain[20], ~Ain[21], ~Ain[22], ~Ain[23], ~Ain[24], ~Ain[25], ~Ain[26], ~Ain[27], ~Ain[28], ~Ain[29], ~Ain[30], Ain[31]);  // And
  and and_2 (and_2_out, We, nor_1_out);
  and and_3 (and_3_out, We, and_1_out);
  RAM_256KB ram_256kb_1 (
    .AddressIn(Ain[17:2]), .Din(Din), .We(and_2_out), .ByteSelect(ByteSelect), .Clock(Clock), .Dout(Dout));
  Terminal terminal_1 (.D(Din), .C(Clock), .en(and_3_out));
endmodule
