// Digital circuit ALU.dig as structural Verilog
module ALU (
  input  [4:0] OPSELECT,
  input  [31:0] B,
  input  [31:0] A,
  input  clock,
  output [31:0] O,
  output [1:0] Flags,
  output stall
);

  wire Adder_c_o, and_1_out, and_2_out, and_4_out, decoder_1_out_1, decoder_1_out_5, decoder_1_out_6,
       decoder_1_out_11, decoder_1_out_13, decoder_1_out_14, decoder_1_out_15, decoder_1_out_16,
       decoder_1_out_17, or_1_out, or_2_out, or_3_out, or_4_out, or_5_out, or_6_out;
  wire [0:0] not_2_out, xor_1_out;
  wire [31:0] Adder_s, and_3_out, full_div_1_o, mul_1_h, mul_1_l, multiplexer_1_out, not_1_out, or_7_out,
       sll_1_out, sra_1_out, srl_1_out, xor_2_out;
  wire [31:1] multiplexer_2_out;

  Decoder #(.Selector_Bits(5)) decoder_1 (
    .sel(OPSELECT), .out_1(decoder_1_out_1), .out_5(decoder_1_out_5), .out_6(decoder_1_out_6),
    .out_11(decoder_1_out_11), .out_13(decoder_1_out_13), .out_14(decoder_1_out_14),
    .out_15(decoder_1_out_15), .out_16(decoder_1_out_16), .out_17(decoder_1_out_17));  // open: out_0, out_2, out_3, out_4, out_7, out_8, out_9, out_10, out_12, out_18, out_19, out_20, out_21, out_22, out_23, out_24, out_25, out_26, out_27, out_28, out_29, out_30, out_31
  or or_1 (or_1_out, decoder_1_out_14, decoder_1_out_16);
  or or_2 (or_2_out, decoder_1_out_16, decoder_1_out_17);
  or or_3 (or_3_out, decoder_1_out_14, decoder_1_out_15, decoder_1_out_16, decoder_1_out_17);
  assign not_1_out = ~B;  // Not not_1, 32 bits wide
  or or_4 (or_4_out, decoder_1_out_1, decoder_1_out_5, decoder_1_out_6);
  or or_5 (or_5_out, decoder_1_out_11, decoder_1_out_13);
  and and_1 (and_1_out, ~A[31], B[31], Adder_s[31]);  // And
  Multiplexer #(.Bits(32)) multiplexer_1 (.sel(or_4_out), .in_0(B), .in_1(not_1_out), .out(multiplexer_1_out));
  or or_6 (or_6_out, and_1_out, and_2_out);
  and and_2 (and_2_out, A[31], ~B[31], ~Adder_s[31]);  // And
  xor xor_1 (xor_1_out[0], or_6_out, Adder_s[31]);
  Add #(.Bits(32)) Adder (.a(A), .b(multiplexer_1_out), .c_i(or_4_out), .s(Adder_s), .c_o(Adder_c_o));
  assign and_3_out = A & multiplexer_1_out;  // And and_3, 32 bits wide
  assign or_7_out = A | multiplexer_1_out;  // Or or_7, 32 bits wide
  assign xor_2_out = A ^ multiplexer_1_out;  // XOr xor_2, 32 bits wide
  SLL sll_1 (.in(A), .shift(multiplexer_1_out[4:0]), .out(sll_1_out));
  SRL srl_1 (.in(A), .shift(multiplexer_1_out[4:0]), .out(srl_1_out));
  SRA sra_1 (.in(A), .shift(multiplexer_1_out[4:0]), .out(sra_1_out));
  mul mul_1 (.A(A), .B(multiplexer_1_out), .As(or_5_out), .Bs(decoder_1_out_11), .L(mul_1_l), .H(mul_1_h));
  full_div full_div_1 (
    .A(A), .B(multiplexer_1_out), .s(or_1_out), .r(or_2_out), .clock(clock), .div(or_3_out),
    .O(full_div_1_o), .stall(stall));
  not not_2 (not_2_out[0], Adder_c_o);
  Multiplexer #(.Bits(32)) multiplexer_2 (
    .sel(and_4_out), .in_0({{31{1'b0}}, not_2_out[0]}), .in_1({{31{1'b0}}, xor_1_out[0]}),
    .out({multiplexer_2_out, Flags[0]}));
  and and_4 (and_4_out, ~OPSELECT[4], ~OPSELECT[3], OPSELECT[2], OPSELECT[1], ~OPSELECT[0]);  // And
  nor nor_1 (Flags[1], Adder_s[31], Adder_s[30], Adder_s[29], Adder_s[28], Adder_s[27], Adder_s[26], Adder_s[25], Adder_s[24], Adder_s[23], Adder_s[22], Adder_s[21], Adder_s[20], Adder_s[19], Adder_s[18], Adder_s[17], Adder_s[16], Adder_s[15], Adder_s[14], Adder_s[13], Adder_s[12], Adder_s[11], Adder_s[10], Adder_s[9], Adder_s[8], Adder_s[7], Adder_s[6], Adder_s[5], Adder_s[4], Adder_s[3], Adder_s[2], Adder_s[1], Adder_s[0]);
  Multiplexer #(.Selector_Bits(5), .Bits(32)) multiplexer_3 (
    .sel(OPSELECT), .in_0(Adder_s), .in_1(Adder_s), .in_2(and_3_out), .in_3(or_7_out), .in_4(xor_2_out),
    .in_5({{31{1'b0}}, not_2_out[0]}), .in_6({{31{1'b0}}, xor_1_out[0]}), .in_7(sll_1_out), .in_8(srl_1_out),
    .in_9(sra_1_out), .in_10(mul_1_l), .in_11(mul_1_h), .in_12(mul_1_h), .in_13(mul_1_h),
    .in_14(full_div_1_o), .in_15(full_div_1_o), .in_16(full_div_1_o), .in_17(full_div_1_o),
    .in_18({32{1'b0}}), .in_19({32{1'b0}}), .in_20({32{1'b0}}), .in_21({32{1'b0}}), .in_22({32{1'b0}}),
    .in_23({32{1'b0}}), .in_24({32{1'b0}}), .in_25({32{1'b0}}), .in_26({32{1'b0}}), .in_27({32{1'b0}}),
    .in_28({32{1'b0}}), .in_29({32{1'b0}}), .in_30({32{1'b0}}), .in_31({32{1'b0}}), .out(O));

  // Notes on the sheet:
  //   OPSELECT: 00000:add
  //   00001:sub
  //   00010:and
  //   00011:or
  //   00100:xor
  //   00101:comUnsigned
  //   00110:comSigned
  //   00111:SLL
  //   01000:SRL
  //   01001:SRA
  //   01010: MUL
  //   01011: MULH
  //   01100: MULHU
  //   01101: MULHSU
  //   01110: DIV
  //   01111: DIVU
  //   10000: REM
  //   10001: REMU
  //   Flags: Z, LessThan
  //   00000:add
  //   00001:sub
  //   00010:and
  //   00011:or
  //   00100:xor
  //   00101:comUnsigned
  //   00110:comSigned
  //   00111:SLL
  //   01000:SRL
  //   01001:SRA
  //   01010: MUL
  //   01011: MULH
  //   01100: MULHU
  //   01101: MULHSU
  //   01110: DIV
  //   01111: DIVU
  //   10000: REM
  //   10001: REMU
endmodule
