// Digital circuit ControlLogic.dig as structural Verilog
module ControlLogic (
  input  [6:0] funct7,
  input  [2:0] funct3,
  input  [6:0] opcode,
  output [2:0] InsTypeSel,
  output [1:0] BrInsSel,
  output [1:0] PCInSel,
  output DSigned,
  output DHalf,
  output DByte,
  output [4:0] ALUOpSel,
  output ALUInSel,
  output [2:0] RegInSel,
  output RegWe,
  output MemWe
);

  wire [4:0] ALUOP_d, multiplexer_1_out;
  wire [5:5] decoder_1_out_1;
  wire [12:11] INS_Logic_d;

  ROM #(.AddrBits(5), .Bits(13)) INS_Logic (
    .A(opcode[6:2]), .sel(1'b1), .D({INS_Logic_d, InsTypeSel, PCInSel, ALUInSel, RegInSel, RegWe, MemWe}));
  Decoder #(.Selector_Bits(2)) decoder_1 (.sel(INS_Logic_d), .out_1(decoder_1_out_1[5]));  // open: out_0, out_2, out_3
  ROM #(.AddrBits(6), .Bits(5)) ALUOP (.A({decoder_1_out_1[5], funct3, funct7[5], funct7[0]}), .sel(1'b1), .D(ALUOP_d));
  Multiplexer #(.Bits(5)) multiplexer_1 (.sel(funct3[1]), .in_0(5'b00110), .in_1(5'b00101), .out(multiplexer_1_out));
  Multiplexer #(.Selector_Bits(2), .Bits(5)) multiplexer_2 (
    .sel(INS_Logic_d), .in_0(ALUOP_d), .in_1(ALUOP_d), .in_2({5{1'b0}}), .in_3(multiplexer_1_out),
    .out(ALUOpSel));
  not not_1 (DSigned, funct3[2]);
  Decoder #(.Selector_Bits(2)) decoder_2 (.sel(funct3[1:0]), .out_0(DByte), .out_1(DHalf));  // open: out_2, out_3

  assign BrInsSel = {funct3[2], funct3[0]};

  // Notes on the sheet:
  //   InsTypeSel: 000: I
  //   001: S
  //   010: B
  //   011: U
  //   100: J
  //   BrInsSel: 00: BEQ
  //   01: BNE
  //   10: BLT
  //   11: BGE
  //   Reg in select
  //   000: ALU
  //   001: RAM
  //   010: PC+4
  //   011: Imm
  //   100: Ad Add
  //   ALU in select
  //   0: rs2
  //   1: Imm
  //   contents of INS_Logic (hex, n*v repeats v):
  //   5*0,312,7*0,30e
  //   PC in select
  //   00: PC+4
  //   01: Ad Adder
  //   10: ALU
  //   11: Con Bra
  //   contents of ALUOP (hex, n*v repeats v):
  //   4*0,7,0,0,0,4*6,4*5,4*4,8,0,9,0,4*3,4*2,0,a,1,0,7,b,0,0,6,d,0,0
  //   ,5,c,0,0,4,e,0,0,8,f,9,0,3,10,0,0,2,11
  //   Ins Type
  //   000: I
  //   001: S
  //   010: B
  //   011: U
  //   100: J
  //   ALU Reg?
  //   ALU op
  //   00: Imm
  //   01: Reg
  //   10: Add
  //   11: Conditional Branch
  //   ALU op
  //   00000:add
  //   00001:sub
  //   00010:and
  //   00011:or
  //   00100:xor
  //   00101:comUnsigned
  //   00110:comSigned
  //   00111:SLL
  //   01000:SRL
  //   01001:SRA
  //   01010: MUL
  //   01011: MULH
  //   01100: MULHU
  //   01101: MULHSU
  //   01110: DIV
  //   01111: DIVU
  //   10000: REM
  //   10001: REMU
endmodule
