// Digital circuit MemoryMapperExp.dig as structural Verilog
module MemoryMapperExp (
  input  Clock,
  input  [31:0] Din,
  input  [31:0] Ain,
  input  [31:0] INSAin,
  input  [3:0] ByteSelect,
  input  We,
  input  [2:0] RegInsel,
  input  [31:0] DrIO,
  output [31:0] INSout,
  output [31:0] Dout,
  output [31:0] AddIO,
  output [31:0] DwIO,
  output WeIO,
  output ReIO,
  output CLKIO
);

  wire and_1_out, decoder_1_out_1;
  wire [2:0] addressspace_1_enable, addressspace_2_enable;
  wire [31:0] INSROM_d, multiplexer_2_out, ram_256kb_1_dout, ram_256kb_1_insout, RROM_d;

  AddressSpace addressspace_1 (.Ain(Ain), .Enable(addressspace_1_enable));
  AddressSpace addressspace_2 (.Ain(INSAin), .Enable(addressspace_2_enable));
  Decoder #(.Selector_Bits(3)) decoder_1 (
    .sel(RegInsel), .out_1(decoder_1_out_1));  // open: out_0, out_2, out_3, out_4, out_5, out_6, out_7
  and and_1 (and_1_out, We, addressspace_1_enable[1]);
  and and_2 (WeIO, We, addressspace_1_enable[2]);
  and and_3 (ReIO, addressspace_1_enable[2], decoder_1_out_1);
  ROM #(.AddrBits(11), .isProgramMemory("true"), .Bits(32)) RROM (.A(Ain[12:2]), .sel(1'b1), .D(RROM_d));
  ROM #(.AddrBits(11), .isProgramMemory("true"), .Bits(32)) INSROM (.A(INSAin[12:2]), .sel(1'b1), .D(INSROM_d));
  RAM_256KB ram_256kb_1 (
    .INSAddressIn(INSAin[17:2]), .ByteSelect(ByteSelect), .AddressIn(Ain[17:2]), .Din(Din), .We(and_1_out),
    .Clock(Clock), .Dout(ram_256kb_1_dout), .INSout(ram_256kb_1_insout));
  Multiplexer #(.Bits(32)) multiplexer_1 (
    .sel(addressspace_2_enable[1]), .in_0(INSROM_d), .in_1(ram_256kb_1_insout), .out(INSout));
  Multiplexer #(.Bits(32)) multiplexer_2 (
    .sel(addressspace_1_enable[1]), .in_0(RROM_d), .in_1(ram_256kb_1_dout), .out(multiplexer_2_out));
  Multiplexer #(.Bits(32)) multiplexer_3 (
    .sel(addressspace_1_enable[2]), .in_0(multiplexer_2_out), .in_1(DrIO), .out(Dout));

  assign AddIO = Ain;
  assign CLKIO = Clock;
  assign DwIO = Din;

  // Notes on the sheet:
  //   RROM loads visual_wozmon.intel.hex
  //   INSROM loads visual_wozmon.intel.hex
endmodule
