// Digital circuit main_cpu_exp.dig as structural Verilog
module main_cpu_exp (
  input  CLK,
  input  [31:0] DrIO,
  output [31:0] AddIO,
  output [31:0] DwIO,
  output WeIO,
  output ReIO,
  output CLKIO
);

  wire controllogic_1_p1, controllogic_1_p2, controllogic_1_p4, datacontroller_1_p3, datacontroller_1_p4,
       datacontroller_1_p5;
  wire [1:0] alu_1_flags, controllogic_1_p9, controllogic_1_p10;
  wire [2:0] controllogic_1_p3, controllogic_1_p11, controllogic_1_p13;
  wire [3:0] datacontroller_1_p8;
  wire [4:0] controllogic_1_p5, instructionsplicer_1_rd, instructionsplicer_1_rs1, instructionsplicer_1_rs2;
  wire [6:0] controllogic_1_p12, controllogic_1_p14;
  wire [31:0] add_1_s, datacontroller_1_p1, datacontroller_1_p2, datacontroller_1_p6, datacontroller_1_p7,
       instructionsplicer_1_imm, memorymapperexp_1_insout, multiplexer_1_out, multiplexer_2_out,
       pcinselector_1_pc, programcounter_1_dout, programcounter_1_pc_plus_4, registers_1_rs1o,
       registers_1_rs2o;

  PcInSelector pcinselector_1 (
    .BranchIns(controllogic_1_p10), .PcInSel(controllogic_1_p9), .Flags(alu_1_flags),
    .ALU(datacontroller_1_p1), .AdAdd(add_1_s), .PC_plus_4(programcounter_1_pc_plus_4), .PC(pcinselector_1_pc));
  // DataController datacontroller_1: pin names not known; wires that end beside it: datacontroller_1_p1, datacontroller_1_p2, datacontroller_1_p3, datacontroller_1_p4, datacontroller_1_p5, datacontroller_1_p6, datacontroller_1_p7, datacontroller_1_p8
  ProgramCounter programcounter_1 (
    .Clock(CLK), .Din(pcinselector_1_pc), .Dout(programcounter_1_dout), .PC_plus_4(programcounter_1_pc_plus_4));
  Add #(.Bits(32)) add_1 (
    .a(instructionsplicer_1_imm), .b(programcounter_1_dout), .c_i(1'b0), .s(add_1_s));  // open: c_o
  ALU alu_1 (
    .OPSELECT(controllogic_1_p5), .B(multiplexer_1_out), .A(registers_1_rs1o), .O(datacontroller_1_p1),
    .Flags(alu_1_flags));
  Multiplexer #(.Bits(32)) multiplexer_1 (
    .sel(controllogic_1_p4), .in_0(registers_1_rs2o), .in_1(instructionsplicer_1_imm), .out(multiplexer_1_out));
  Multiplexer #(.Selector_Bits(3), .Bits(32)) multiplexer_2 (
    .sel(controllogic_1_p3), .in_0(datacontroller_1_p1), .in_1(datacontroller_1_p7),
    .in_2(programcounter_1_pc_plus_4), .in_3(instructionsplicer_1_imm), .in_4(add_1_s), .in_5({32{1'b0}}),
    .in_6({32{1'b0}}), .in_7({32{1'b0}}), .out(multiplexer_2_out));
  Registers registers_1 (
    .clk(CLK), .Din(multiplexer_2_out), .We(controllogic_1_p2), .rs1(instructionsplicer_1_rs1),
    .rs2(instructionsplicer_1_rs2), .rd(instructionsplicer_1_rd), .rs1O(registers_1_rs1o),
    .rs2O(registers_1_rs2o));
  MemoryMapperExp memorymapperexp_1 (
    .Clock(CLK), .Din(registers_1_rs2o), .Ain(datacontroller_1_p6), .INSAin(programcounter_1_dout),
    .ByteSelect(datacontroller_1_p8), .We(controllogic_1_p1), .RegInsel(controllogic_1_p3), .DrIO(DrIO),
    .INSout(memorymapperexp_1_insout), .Dout(datacontroller_1_p2), .AddIO(AddIO), .DwIO(DwIO), .WeIO(WeIO),
    .ReIO(ReIO), .CLKIO(CLKIO));
  // ControlLogic controllogic_1: pin names not known; wires that end beside it: controllogic_1_p1, controllogic_1_p2, controllogic_1_p3, controllogic_1_p4, controllogic_1_p5, datacontroller_1_p5, datacontroller_1_p4, datacontroller_1_p3, controllogic_1_p9, controllogic_1_p10, controllogic_1_p11, controllogic_1_p12, controllogic_1_p13, controllogic_1_p14
  InstructionSplicer instructionsplicer_1 (
    .ImmSel(controllogic_1_p11), .INSin(memorymapperexp_1_insout), .funct7(controllogic_1_p14),
    .funct3(controllogic_1_p13), .opcode(controllogic_1_p12), .rs1(instructionsplicer_1_rs1),
    .rs2(instructionsplicer_1_rs2), .rd(instructionsplicer_1_rd), .Imm(instructionsplicer_1_imm));

  // Notes on the sheet:
  //   CLK: Hz: 75000
  //   PC Lines
  //   Data Controller Lines
  //   ALU Lines
  //   Register Lines
  //   Memory Mapper Lines
endmodule
